// Logisim project da1_task3.circ as structural Verilog: 3 circuits, main circuit DUT
module DUT (
  input  X,
  input  CLK,
  input  RST,
  output Z
);


  // Notes on the sheet:
  //   Please put your deisgn below. You may also use subcircuits.
  //   However, do not move, rename, add, or delete any pins.
  //   Put your design below and wire it up to the pins.
  //   Feel free to remove this text.
endmodule

module TB (
);

  wire clk_out, mypor_1_p2, not_1_out, or_1_out, RESET_out, TimeIndex_carry, undriven;
  wire [0:0] dut_1_z;
  wire [4:0] TimeIndex_q;

  Clock #(.highDuration(2), .lowDuration(2)) clk (.out(clk_out));
  Clock sysclk ();  // open: out
  Counter #(.max('h1f), .ongoal("stay"), .width(5)) TimeIndex (
    .load(or_1_out), .clk(clk_out), .D({5{1'b0}}), .carry(TimeIndex_carry), .Q(TimeIndex_q));  // open: clr, up, count
  // MyPOR mypor_1: pin names not known; wires that end beside it: clk_out, mypor_1_p2
  Button RESET (.out(RESET_out));
  ROM #(.addrWidth(5), .dataWidth(1)) TestTraceMemory (.addr(TimeIndex_q));  // open: data
  or or_1 (or_1_out, mypor_1_p2, RESET_out);
  not not_1 (not_1_out, TimeIndex_carry);
  DUT dut_1 (.X(undriven), .CLK(clk_out), .RST(or_1_out), .Z(dut_1_z[0]));
  TTY tty_1 (.data({6'b011000, dut_1_z[0]}), .clk(clk_out), .we(not_1_out), .clr(or_1_out));
  LED DONE (.in(TimeIndex_carry));

  // Notes on the sheet:
  //   DO NOT MODIFY THIS
  //   YOU MAY TEST YOUR CIRCUITS USING THIS TO MAKE SURE YOU HAVE NOT ALTERED PIN OUT
  //   Edit ROM with input trace of 32 bits
endmodule

module TBRANDOM (
);

  wire clk_out, mypor_1_p2, not_1_out, or_1_out, random_1_out, RESET_out, TimeIndex_carry;
  wire [0:0] dut_1_z;

  Clock #(.highDuration(2), .lowDuration(2)) clk (.out(clk_out));
  Clock sysclk ();  // open: out
  Counter #(.ongoal("stay")) TimeIndex (
    .load(or_1_out), .clk(clk_out), .D({8{1'b0}}), .carry(TimeIndex_carry));  // open: clr, up, count, Q
  // MyPOR mypor_1: pin names not known; wires that end beside it: clk_out, mypor_1_p2
  Button RESET (.out(RESET_out));
  or or_1 (or_1_out, mypor_1_p2, RESET_out);
  Random #(.width(1)) random_1 (.clr(or_1_out), .clk(clk_out), .out(random_1_out));  // open: next
  not not_1 (not_1_out, TimeIndex_carry);
  DUT dut_1 (.X(random_1_out), .CLK(clk_out), .RST(or_1_out), .Z(dut_1_z[0]));
  TTY tty_1 (.data({6'b011000, dut_1_z[0]}), .clk(clk_out), .we(not_1_out), .clr(or_1_out));
  LED DONE (.in(TimeIndex_carry));

  // Notes on the sheet:
  //   DO NOT MODIFY THIS
  //   YOU MAY TEST YOUR CIRCUITS USING THIS TO MAKE SURE YOU HAVE NOT ALTERED PIN OUT
endmodule
